// Logisim project assignment.circ as structural Verilog: 5 circuits, main circuit main
module main (
);

  wire alu_1_neg, clock_1_out, cu_1_alusrc, cu_1_jump_sel, cu_1_memtoreg, cu_1_memwrite, cu_1_regwrite,
       RESET_out;
  wire [2:0] cu_1_op;
  wire [7:0] alu_1_result, bit_extender_1_out, IR_q, IR_q_2, multiplexer_1_out, multiplexer_2_out,
       pc_1_pc_out, ram_1_data, register_file_1_rd_a_out, register_file_1_rd_b_out;
  wire [15:0] rom_1_data;

  Clock clock_1 (.out(clock_1_out));
  Button RESET (.out(RESET_out));
  PC pc_1 (.JUMP_ADDR(IR_q), .CLK(clock_1_out), .JUMP_SEL(cu_1_jump_sel), .RST(RESET_out), .PC_OUT(pc_1_pc_out));
  ROM #(.dataWidth(16)) rom_1 (.addr(pc_1_pc_out), .data(rom_1_data));  // open: sel
  assign bit_extender_1_out = {{5{1'b0}}, IR_q[2:0]};  // Bit_Extender bit_extender_1
  Register #(.width(16)) IR (.D(rom_1_data), .Q({IR_q_2, IR_q}), .clk(clock_1_out), .clr(RESET_out));  // open: en
  Multiplexer #(.width(8)) multiplexer_1 (
    .in0(register_file_1_rd_b_out), .in1(bit_extender_1_out), .out(multiplexer_1_out), .sel(cu_1_alusrc));  // open: en
  Register_File register_file_1 (
    .WR_DATA(multiplexer_2_out), .WR_EN(cu_1_regwrite), .WR_ADDR(IR_q_2[3:1]), .CLK(clock_1_out),
    .RD_B(IR_q[5:3]), .RD_A_OUT(register_file_1_rd_a_out), .RD_A({IR_q_2[0], IR_q[7:6]}),
    .RD_B_OUT(register_file_1_rd_b_out));
  CU cu_1 (
    .NEG(alu_1_neg), .OPCODE(IR_q_2[7:4]), .OP(cu_1_op), .JUMP_SEL(cu_1_jump_sel), .RegWrite(cu_1_regwrite),
    .MemToReg(cu_1_memtoreg), .AluSrc(cu_1_alusrc), .MemWrite(cu_1_memwrite));
  RAM #(.bus("separate")) ram_1 (
    .addr(alu_1_result), .din(register_file_1_rd_b_out), .data(ram_1_data), .str(cu_1_memwrite),
    .clk(clock_1_out), .ld(1'b1), .clr(RESET_out));  // open: sel
  ALU alu_1 (
    .A(register_file_1_rd_a_out), .B(multiplexer_1_out), .CLK(clock_1_out), .OP(cu_1_op),
    .RESULT(alu_1_result), .NEG(alu_1_neg));
  Multiplexer #(.width(8)) multiplexer_2 (
    .in0(alu_1_result), .in1(ram_1_data), .out(multiplexer_2_out), .sel(cu_1_memtoreg));  // open: en

  // Notes on the sheet:
  //   contents of rom_1 (hex, n*v repeats v):
  //   0 1200 ba07 b602 4b58 bc01 4400 60a8 800a 7010 4610 48f0 1900 20e0 44b0 7007 2148 7001
endmodule

module PC (
  input  [7:0] JUMP_ADDR,
  input  CLK,
  input  JUMP_SEL,
  input  RST,
  output [7:0] PC_OUT
);

  wire [7:0] adder_1_out, register_1_q;

  Register register_1 (.D(PC_OUT), .Q(register_1_q), .clk(CLK), .clr(RST));  // open: en
  Adder adder_1 (.a(register_1_q), .b(8'h1), .out(adder_1_out));  // open: cin, cout
  Multiplexer #(.width(8)) multiplexer_1 (
    .in0(adder_1_out), .in1(JUMP_ADDR), .out(PC_OUT), .sel(JUMP_SEL));  // open: en
endmodule

// Reg
module Register_File (
  input  [7:0] WR_DATA,
  input  [2:0] RD_A,
  input  WR_EN,
  input  [2:0] WR_ADDR,
  input  CLK,
  input  [2:0] RD_B,
  output [7:0] RD_A_OUT,
  output [7:0] RD_B_OUT
);

  wire decoder_1_out0, decoder_1_out1, decoder_1_out2, decoder_1_out3, decoder_1_out4, decoder_1_out5,
       decoder_1_out6, decoder_1_out7;
  wire [7:0] R0_q, R1_q, R2_q, R3_q, R4_q, R5_q, R6_q, R7_q;

  Decoder #(.select(3), .disabled(0)) decoder_1 (
    .out0(decoder_1_out0), .out1(decoder_1_out1), .out2(decoder_1_out2), .out3(decoder_1_out3),
    .out4(decoder_1_out4), .out5(decoder_1_out5), .out6(decoder_1_out6), .out7(decoder_1_out7),
    .sel(WR_ADDR), .en(WR_EN));
  Register R0 (.D(WR_DATA), .en(decoder_1_out0), .Q(R0_q), .clk(CLK));  // open: clr
  Register R1 (.D(WR_DATA), .en(decoder_1_out1), .Q(R1_q), .clk(CLK));  // open: clr
  Register R2 (.D(WR_DATA), .en(decoder_1_out2), .Q(R2_q), .clk(CLK));  // open: clr
  Register R3 (.D(WR_DATA), .en(decoder_1_out3), .Q(R3_q), .clk(CLK));  // open: clr
  Register R4 (.D(WR_DATA), .en(decoder_1_out4), .Q(R4_q), .clk(CLK));  // open: clr
  Register R5 (.D(WR_DATA), .en(decoder_1_out5), .Q(R5_q), .clk(CLK));  // open: clr
  Register R6 (.D(WR_DATA), .en(decoder_1_out6), .Q(R6_q), .clk(CLK));  // open: clr
  Register R7 (.D(WR_DATA), .en(decoder_1_out7), .Q(R7_q), .clk(CLK));  // open: clr
  Multiplexer #(.select(3), .width(8)) multiplexer_1 (
    .in0(R0_q), .in1(R1_q), .in2(R2_q), .in3(R3_q), .in4(R4_q), .in5(R5_q), .in6(R6_q), .in7(R7_q),
    .out(RD_A_OUT), .sel(RD_A));  // open: en
  Multiplexer #(.select(3), .width(8)) multiplexer_2 (
    .in0(R0_q), .in1(R1_q), .in2(R2_q), .in3(R3_q), .in4(R4_q), .in5(R5_q), .in6(R6_q), .in7(R7_q),
    .out(RD_B_OUT), .sel(RD_B));  // open: en
endmodule

module ALU (
  input  [7:0] A,
  input  [7:0] B,
  input  CLK,
  input  [2:0] OP,
  output [7:0] RESULT,
  output NEG
);

  wire [7:0] adder_1_out, and_1_out, not_1_out, or_1_out, subtractor_1_out;

  Adder adder_1 (.a(A), .b(B), .out(adder_1_out));  // open: cin, cout
  Subtractor subtractor_1 (.a(A), .b(B), .out(subtractor_1_out));  // open: bin, bout
  assign not_1_out = ~A;  // NOT_Gate not_1, 8 bits wide
  assign and_1_out = A & B;  // AND_Gate and_1, 8 bits wide
  assign or_1_out = A | B;  // OR_Gate or_1, 8 bits wide
  Multiplexer #(.select(3), .width(8)) multiplexer_1 (
    .in0(adder_1_out), .in1(subtractor_1_out), .in2(and_1_out), .in3(or_1_out), .in4(not_1_out), .in5(A),
    .in6(B), .out(RESULT), .sel(OP));  // open: in7, en
  D_Flip_Flop d_ff_1 (.clk(CLK), .D(RESULT[7]), .Q(NEG));  // open: Qn, preset, en, reset
endmodule

module CU (
  input  [3:0] OPCODE,
  input  NEG,
  output [2:0] OP,
  output JUMP_SEL,
  output RegWrite,
  output MemToReg,
  output AluSrc,
  output MemWrite
);

  wire ADD_out, and_1_out, JLT_out, JMP_out, LOAD_out, LOADX_out, MOV_out, MOVC_out, not_1_out, not_2_out,
       not_3_out, not_4_out, STORE_out, STRX_out, SUB_out;

  not not_1 (not_1_out, OPCODE[3]);
  not not_2 (not_2_out, OPCODE[2]);
  not not_3 (not_3_out, OPCODE[1]);
  not not_4 (not_4_out, OPCODE[0]);
  and JMP (JMP_out, OPCODE[0], OPCODE[1], OPCODE[2], not_1_out);
  and JLT (JLT_out, not_4_out, not_3_out, not_2_out, OPCODE[3]);
  and LOAD (LOAD_out, OPCODE[0], not_3_out, not_2_out, not_1_out);
  and MOV (MOV_out, OPCODE[0], OPCODE[1], not_2_out, not_1_out);
  and ADD (ADD_out, not_4_out, not_3_out, OPCODE[2], not_1_out);
  and SUB (SUB_out, OPCODE[0], not_3_out, OPCODE[2], not_1_out);
  and MOVC (MOVC_out, OPCODE[0], OPCODE[1], not_2_out, OPCODE[3]);
  and LOADX (LOADX_out, OPCODE[0], not_3_out, not_2_out, OPCODE[3]);
  and STRX (STRX_out, not_4_out, OPCODE[1], not_2_out, OPCODE[3]);
  and STORE (STORE_out, not_4_out, OPCODE[1], not_2_out, not_1_out);
  and and_1 (and_1_out, JLT_out, NEG);
  or or_1 (JUMP_SEL, JMP_out, and_1_out);
  or or_2 (RegWrite, LOAD_out, MOV_out, ADD_out, SUB_out, MOVC_out, LOADX_out);
  or or_3 (MemWrite, STRX_out, STORE_out);
  or or_4 (MemToReg, LOAD_out, LOADX_out);
  or or_5 (AluSrc, MOVC_out, LOADX_out, STRX_out);
  Multiplexer #(.select(4), .width(3)) multiplexer_1 (
    .in0(3'b000), .in1(3'b101), .in2(3'b101), .in3(3'b101), .in4(3'b000), .in5(3'b001), .in6(3'b001),
    .in7(3'b000), .in8(3'b000), .in9(3'b000), .in10(3'b000), .in11(3'b110), .in12(3'b000), .in13(3'b000),
    .in14(3'b000), .in15(3'b000), .out(OP), .sel(OPCODE));  // open: en
endmodule
